# Fritzing sketch lan (saved by Fritzing 0.9.2b)
breadboards: 1

parts:
  Bauteil1 = Arduino Nano (Rev3.0)
  Bauteil2 = ENC28J60 Breakout Board

nets:
  GND: Bauteil1.GND, Bauteil2.GND
  N1: Bauteil1.D8, Bauteil2.CS
  N2: Bauteil1.D11/MOSI, Bauteil2.SI
  N3: Bauteil1.D12/MISO, Bauteil2.SO
  3V3: Bauteil1.3V3, Bauteil2.VCC
  N4: Bauteil1.D13/SCK, Bauteil2.SCK

custom parts:
  ENC28J60 Breakout Board: This is a breakout board for the Microchip ENC28J60 stand-alone ethernet controller. The ENC28J60 has an SPI interface. It operates at 3.3 Volts.
