# Fritzing sketch ledstrip (saved by Fritzing 0.9.2b)
breadboards: 1

parts:
  Bauteil1 = Arduino Nano (Rev3.0)
  Bauteil2 = ENC28J60 Breakout Board
  Analog_RGB_LED_Strip1 = Analog RGB LED Strip
  Q1 = TIP120 Hi-Current Darlington Transistor
  Q2 = TIP120 Hi-Current Darlington Transistor
  Q3 = TIP120 Hi-Current Darlington Transistor
  R3 = Resistor [tolerance=±5% resistance=220 package=THT]
  Power_plug1 = Power plug
  R5 = Resistor [tolerance=±5% resistance=220 package=THT]
  R6 = Resistor [tolerance=±5% resistance=220 package=THT]

nets:
  GND: Bauteil1.GND, Bauteil2.GND
  N1: Bauteil1.D3, R5.Pin_1
  N2: Bauteil1.D5, R3.Pin_1
  N3: Bauteil1.D6, R6.Pin_1
  N4: Bauteil1.D8, Bauteil2.CS
  N5: Bauteil1.D11/MOSI, Bauteil2.SI
  N6: Bauteil1.D12/MISO, Bauteil2.SO
  3V3: Bauteil1.3V3, Bauteil2.VCC
  N7: Bauteil1.D13/SCK, Bauteil2.SCK
  12V: Analog_RGB_LED_Strip1.12v, Power_plug1.GND
  N8: Analog_RGB_LED_Strip1.G, Q1.COLLECTOR
  N9: Analog_RGB_LED_Strip1.R, Q2.COLLECTOR
  N10: Analog_RGB_LED_Strip1.B, Q3.COLLECTOR
  N11: Q1.BASE, R6.Pin_0
  N12: Q1.EMITTER, Q2.EMITTER, Q3.EMITTER, Power_plug1.VCC
  N13: Q2.BASE, R3.Pin_0
  N14: Q3.BASE, R5.Pin_0

custom parts:
  ENC28J60 Breakout Board: This is a breakout board for the Microchip ENC28J60 stand-alone ethernet controller. The ENC28J60 has an SPI interface. It operates at 3.3 Volts.
  Analog RGB LED Strip: Analog RGB LED strip
