# Fritzing sketch tip120 (saved by Fritzing 0.9.2b)
breadboards: 1

parts:
  Bauteil1 = Arduino Nano (Rev3.0)  # not connected
  Q1 = TIP120 Hi-Current Darlington Transistor
  Analog_RGB_LED_Strip1 = Analog RGB LED Strip
  R1 = Resistor [tolerance=±5% resistance=220 package=THT]
  Power_plug1 = Power plug

nets:
  N1: Q1.BASE, R1.Pin_1
  N2: Q1.COLLECTOR, Analog_RGB_LED_Strip1.G
  N3: Q1.EMITTER, Power_plug1.GND
  12V: Analog_RGB_LED_Strip1.12v, Power_plug1.VCC

custom parts:
  Analog RGB LED Strip: Analog RGB LED strip
